# Fritzing sketch ESP8266-programmer (saved by Fritzing 0.9.4)
circuit board: 8cm x 6cm
breadboards: 1

parts:
  ESP-12F = Gizwits WiFi Witty ESP-12F
  RESET_SW = Pushbutton [package="[THT]"]
  R2 = Resistor [tolerance=±5% resistance=10k package=THT]
  J1_ESP-01 = ESP-01 Socket - 8 pins [form="♀ (female)" package=THT]
  J2_CH430 = CH430 - 8 pins [form="♀ (female)" package=THT]
  FLASH_SW = Pushbutton [package="[THT]"]
  J3_Aux_Power = female pin header, 2 pins [form="♀ (female)"]
  PWR_SW = Toggle Switch [package=THT]

nets:
  N1: ESP-12F.REST, RESET_SW.Pin_1, RESET_SW.Pin_2, R2.Pin_1, J1_ESP-01.pin6
  N2: ESP-12F.CH_PD, ESP-12F.VCC, R2.Pin_0, J1_ESP-01.pin4, J1_ESP-01.pin8, PWR_SW.COM
  N3: ESP-12F.GND, RESET_SW.Pin_3, RESET_SW.Pin_4, J1_ESP-01.pin1, J2_CH430.pin1, FLASH_SW.Pin_1, J3_Aux_Power.pin1
  N4: ESP-12F.GPIO0, J1_ESP-01.pin5, FLASH_SW.Pin_3, FLASH_SW.Pin_4
  N5: ESP-12F.RXD, J1_ESP-01.pin7, J2_CH430.pin7
  N6: ESP-12F.TXD, J1_ESP-01.pin2, J2_CH430.pin2
  N7: J2_CH430.pin8, PWR_SW.L2
  N8: J3_Aux_Power.pin2, PWR_SW.L1

notes:
  ESP-12F/01 Programmer Board

custom parts:
  ESP-01 Socket - 8 pins: Generic double row female header
  CH430 - 8 pins: Generic double row male header
