# Fritzing sketch ESP8266-programmer (saved by Fritzing 0.9.4)
circuit board: 7cm x 5.7cm
breadboards: 1

parts:
  ESP-12F = Gizwits WiFi Witty ESP-12F
  S1 = Pushbutton [package="[THT]"]
  R2 = Resistor [tolerance=±5% resistance=10k package=THT]
  J1_ESP-01 = ESP-01 Socket - 8 pins [form="♀ (female)" package=THT]
  J2_CH430 = CH430 - 8 pins [form="♀ (female)" package=THT]
  S2 = Pushbutton [package="[THT]"]
  R3 = Resistor [tolerance=±5% resistance=10k package=THT]
  J3 = female pin header, 2 pins [form="♀ (female)"]
  R1 = Resistor [tolerance=±5% resistance=10k package=THT]
  R5 = Resistor [tolerance=±5% resistance=10k package=THT]
  R4 = Resistor [tolerance=±5% resistance=10k package=THT]
  C1 = Electrolytic Capacitor [capacitance=1000µF package="200 mil [THT, electrolytic]"]
  C2 = Ceramic Capacitor [capacitance=100nF package="200 mil [THT, multilayer]"]

nets:
  REST: ESP-12F.REST, S1.Pin_1, S1.Pin_2, R2.Pin_1, J1_ESP-01.pin6
  CH_PD: ESP-12F.CH_PD, J1_ESP-01.pin4, R3.Pin_1
  3.3V: ESP-12F.VCC, R2.Pin_0, J1_ESP-01.pin8, R3.Pin_0, J3.pin1, R5.Pin_0, R4.Pin_0, C1.+, C2.1
  GND: ESP-12F.GND, S1.Pin_3, S1.Pin_4, J1_ESP-01.pin1, J2_CH430.pin1, S2.Pin_1, S2.Pin_2, J3.pin2, R1.Pin_1, C1.-, C2.0
  N1: ESP-12F.GPIO15, R1.Pin_0
  GPIO2: ESP-12F.GPIO2, R4.Pin_1
  GPIO0: ESP-12F.GPIO0, J1_ESP-01.pin5, S2.Pin_3, R5.Pin_1
  RXD: ESP-12F.RXD, J1_ESP-01.pin7, J2_CH430.pin7
  TXD: ESP-12F.TXD, J1_ESP-01.pin2, J2_CH430.pin2

custom parts:
  ESP-01 Socket - 8 pins: Generic double row female header
  CH430 - 8 pins: Generic double row male header
